// Logisim project Bin-to-GC-to-BCD-to-7seg_Logisim.circ as structural Verilog: 1 circuit, main circuit Binary to Grade Code to BCD / 7-Segment - Only MUX, Dec, Enc
module Binary_to_Grade_Code_to_BCD___7_Segment___Only_MUX__Dec__Enc (
  output W,
  output X,
  output Y,
  output Z,
  output A,
  output B,
  output C,
  output D,
  output B4,
  output B3,
  output B2,
  output B1,
  output B0
);

  wire clock_1_out, decoder_1_out0, decoder_1_out1, decoder_1_out2, decoder_1_out3, decoder_1_out4,
       decoder_1_out5, decoder_1_out6, decoder_1_out7, decoder_1_out8, decoder_1_out9, decoder_1_out10,
       decoder_1_out11, decoder_1_out12, decoder_1_out13, decoder_1_out14, decoder_1_out15,
       multiplexer_1_out, multiplexer_2_out, multiplexer_3_out, multiplexer_4_out, multiplexer_5_out,
       multiplexer_6_out, multiplexer_7_out, multiplexer_9_out, multiplexer_10_out, multiplexer_11_out,
       multiplexer_13_out, multiplexer_14_out, multiplexer_17_out, multiplexer_18_out, not_1_out, not_2_out,
       not_3_out, not_4_out;

  Clock clock_1 (.out(clock_1_out));
  T_Flip_Flop #(.trigger("falling")) t_ff_1 (.clk(clock_1_out), .T(1'b1), .Q(D));  // open: Qn, preset, reset, en
  T_Flip_Flop #(.trigger("falling")) t_ff_2 (.clk(D), .T(1'b1), .Q(C));  // open: Qn, preset, reset, en
  Multiplexer #(.select(3), .enable("false")) multiplexer_1 (
    .in0(1'b0), .in1(1'b1), .in2(1'b1), .in3(not_1_out), .in4(1'b1), .out(multiplexer_1_out), .sel(3'b000));  // open: in5, in6, in7
  T_Flip_Flop #(.trigger("falling")) t_ff_3 (.clk(C), .T(1'b1), .Q(B));  // open: Qn, preset, reset, en
  Multiplexer #(.select(3), .enable("false")) multiplexer_2 (
    .in0(not_1_out), .in1(1'b1), .in2(B4), .in3(1'b1), .in4(1'b1), .out(multiplexer_2_out), .sel(3'b000));  // open: in5, in6, in7
  Multiplexer #(.select(3), .enable("false")) multiplexer_3 (
    .in0(not_1_out), .in1(1'b0), .in2(1'b1), .in3(not_1_out), .in4(1'b1), .out(multiplexer_3_out),
    .sel(3'b000));  // open: in5, in6, in7
  T_Flip_Flop #(.trigger("falling")) t_ff_4 (.clk(B), .T(1'b1), .Q(A));  // open: Qn, preset, reset, en
  Multiplexer #(.select(3), .enable("false")) multiplexer_4 (
    .in0(1'b1), .in1(1'b1), .in2(not_1_out), .in3(B4), .in4(1'b1), .out(multiplexer_4_out), .sel(3'b000));  // open: in5, in6, in7
  Multiplexer #(.select(3), .enable("false")) multiplexer_5 (
    .in0(not_1_out), .in1(not_1_out), .in2(1'b0), .in3(not_1_out), .in4(not_1_out), .out(multiplexer_5_out),
    .sel(3'b000));  // open: in5, in6, in7
  not not_1 (not_1_out, B4);
  Multiplexer #(.select(3), .enable("false")) multiplexer_6 (
    .in0(1'b1), .in1(B4), .in2(1'b1), .in3(1'b1), .in4(1'b1), .out(multiplexer_6_out), .sel(3'b000));  // open: in5, in6, in7
  _7_Segment_Display u_7_segment_display_1 (
    .g(multiplexer_1_out), .f(multiplexer_3_out), .a(multiplexer_2_out), .b(multiplexer_4_out),
    .e(multiplexer_5_out), .d(multiplexer_7_out), .c(multiplexer_6_out));  // open: dp
  _7_Segment_Display u_7_segment_display_2 (
    .g(multiplexer_9_out), .f(multiplexer_11_out), .a(multiplexer_10_out), .b(multiplexer_13_out),
    .e(multiplexer_14_out), .d(multiplexer_18_out), .c(multiplexer_17_out));  // open: dp
  Multiplexer #(.select(3), .enable("false")) multiplexer_7 (
    .in0(not_1_out), .in1(1'b1), .in2(B4), .in3(not_1_out), .in4(1'b1), .out(multiplexer_7_out), .sel(3'b000));  // open: in5, in6, in7
  Multiplexer #(.select(3), .enable("false")) multiplexer_8 (
    .in0(1'b0), .in1(1'b0), .in2(1'b0), .in3(1'b0), .in4(1'b1), .in5(1'b1), .in6(1'b1), .in7(1'b1), .out(W),
    .sel({A, B, C}));
  Multiplexer #(.select(3), .enable("false")) multiplexer_9 (
    .in0(1'b0), .in1(1'b1), .in2(1'b1), .in3(not_4_out), .in4(1'b1), .out(multiplexer_9_out),
    .sel({B3, B2, B1}));  // open: in5, in6, in7
  Multiplexer #(.select(3), .enable("false")) multiplexer_10 (
    .in0(not_3_out), .in1(1'b1), .in2(B0), .in3(1'b1), .in4(1'b1), .out(multiplexer_10_out),
    .sel({B3, B2, B1}));  // open: in5, in6, in7
  Multiplexer #(.select(3), .enable("false")) multiplexer_11 (
    .in0(not_4_out), .in1(1'b0), .in2(1'b1), .in3(not_4_out), .in4(1'b1), .out(multiplexer_11_out),
    .sel({B3, B2, B1}));  // open: in5, in6, in7
  Multiplexer #(.select(3), .enable("false")) multiplexer_12 (
    .in0(1'b0), .in1(1'b0), .in2(1'b1), .in3(1'b1), .in4(1'b1), .in5(1'b1), .in6(1'b0), .in7(1'b0), .out(X),
    .sel({A, B, C}));
  Multiplexer #(.select(3), .enable("false")) multiplexer_13 (
    .in0(1'b1), .in1(1'b1), .in2(not_3_out), .in3(B0), .in4(1'b1), .out(multiplexer_13_out),
    .sel({B3, B2, B1}));  // open: in5, in6, in7
  Multiplexer #(.select(3), .enable("false")) multiplexer_14 (
    .in0(not_4_out), .in1(not_4_out), .in2(1'b0), .in3(not_4_out), .in4(not_4_out), .out(multiplexer_14_out),
    .sel({B3, B2, B1}));  // open: in5, in6, in7
  Multiplexer #(.select(3), .enable("false")) multiplexer_15 (
    .in0(1'b0), .in1(1'b1), .in2(1'b1), .in3(1'b0), .in4(1'b0), .in5(1'b1), .in6(1'b1), .in7(1'b0), .out(Y),
    .sel({A, B, C}));
  Multiplexer #(.select(3), .enable("false")) multiplexer_16 (
    .in0(D), .in1(not_2_out), .in2(D), .in3(not_2_out), .in4(D), .in5(not_2_out), .in6(D), .in7(not_2_out),
    .out(Z), .sel({A, B, C}));
  not not_2 (not_2_out, D);
  not not_3 (not_3_out, B0);
  Multiplexer #(.select(3), .enable("false")) multiplexer_17 (
    .in0(1'b1), .in1(B0), .in2(1'b1), .in3(1'b1), .in4(1'b1), .out(multiplexer_17_out), .sel({B3, B2, B1}));  // open: in5, in6, in7
  Multiplexer #(.select(3), .enable("false")) multiplexer_18 (
    .in0(not_4_out), .in1(1'b1), .in2(B0), .in3(not_4_out), .in4(1'b1), .out(multiplexer_18_out),
    .sel({B3, B2, B1}));  // open: in5, in6, in7
  not not_4 (not_4_out, B0);
  Decoder #(.select(4), .enable("false")) decoder_1 (
    .out0(decoder_1_out0), .out1(decoder_1_out1), .out2(decoder_1_out2), .out3(decoder_1_out3),
    .out4(decoder_1_out4), .out5(decoder_1_out5), .out6(decoder_1_out6), .out7(decoder_1_out7),
    .out8(decoder_1_out8), .out9(decoder_1_out9), .out10(decoder_1_out10), .out11(decoder_1_out11),
    .out12(decoder_1_out12), .out13(decoder_1_out13), .out14(decoder_1_out14), .out15(decoder_1_out15),
    .sel({W, X, Y, Z}));
  // Priority_Encoder #(.select(5)) priority_encoder_1: pin names not known; wires that end beside it: 1'b1, 1'b0, 1'b0, 1'b1, decoder_1_out0, decoder_1_out1, decoder_1_out3, decoder_1_out2, decoder_1_out6, decoder_1_out7, decoder_1_out5, decoder_1_out4, decoder_1_out12, decoder_1_out13, {B4, B3, B2, B1, B0}, decoder_1_out15, decoder_1_out14, decoder_1_out10, decoder_1_out11, decoder_1_out9, decoder_1_out8

  // Notes on the sheet:
  //   Combinational Circuit
  //   By Kim Ficara, 104491133
  //   & Zach Shaver, 104425444
  //   Unused BCD
  //   Binary to Gray Code to BCD / 7-Segment
  //   Binary Count
  //   7-Segment Output
  //   (Logic 1)
  //   (Logic 0)
  //   ~B0
  //   ~B4
  //   B0
  //   B4
  //   B0
  //   B4
  //   ~B0
  //   ~B4
  //   Gray Code Output
  //   1
  //   0
  //   0
  //   1
  //   BCD Output
  //   Grey Code to BCD
  //   <- Converter
endmodule
